# Fritzing sketch ArduinoNano-ENC28J60-DualRelay5V (saved by Fritzing 0.9.3b)
breadboards: 1

parts:
  5_Volt_USB = Power plug
  U2 = 2-Channel 5v Relay Shield [package=relay-2ch5v10a]
  Garage_Light = Momentary Switch [package=ksa_sealed_tac_switch]
  Garage_Switch = Momentary Switch [package=ksa_sealed_tac_switch]
  ENC28J1 = ENC28J60
  Arduino_Nano_v3 = Arduino Nano (Rev3.0)

nets:
  GND: 5_Volt_USB.GND, U2.GND, ENC28J1.GND, Arduino_Nano_v3.GND
  VCC: 5_Volt_USB.VCC, U2.VCC, ENC28J1.5v, Arduino_Nano_v3.VIN
  N1: U2.IN1, Arduino_Nano_v3.D2
  N2: U2.IN2, Arduino_Nano_v3.D3
  N3: U2.K1-In, Garage_Switch.1
  N4: U2.K1-Off, Garage_Switch.2
  N5: U2.K1-On, U2.K2-On
  N6: U2.K2-In, Garage_Light.1
  N7: U2.K2-Off, Garage_Light.2
  N8: ENC28J1.INT, ENC28J1.SO, Arduino_Nano_v3.D12/MISO
  N9: ENC28J1.SCK, Arduino_Nano_v3.D13/SCK
  N10: ENC28J1.SI, Arduino_Nano_v3.D11/MOSI
  N11: ENC28J1.CS, Arduino_Nano_v3.D10

custom parts:
  2-Channel 5v Relay Shield: 2 Channel 5v Relay Shield w. 2x SPD-06VDC-SD-C
  ENC28J60: Ethernet Module ENC28J60
