# Fritzing sketch IRSender5V (saved by Fritzing 0.9.3b)
breadboards: 1

parts:
  5_Volts = Power plug
  Part1 = SparkFun ESP8266 Thing
  LED3 = smd LED [color="Infrared (940nm)" package="0805 [SMD]"]
  TSAL6400 = smd LED [color="Infrared (940nm)" package="0805 [SMD]"]
  LED4 = smd LED [color="Infrared (940nm)" package="0805 [SMD]"]
  R1 = Resistor [tolerance=±5% resistance=22 package="2010 [SMD]"]  # not connected

nets:
  GND: 5_Volts.GND, Part1.GND
  VCC: 5_Volts.VCC, Part1.VIN
  N1: Part1.GPIO4, TSAL6400.cathode
  N2: LED3.cathode, LED4.anode
  N3: TSAL6400.anode, LED4.cathode
